// Logisim project circuito.circ as structural Verilog: 5 circuits, main circuit Project
module Project (
  input  rst,
  input  clk,
  input  start,
  input  [7:0] valor,
  output overflow,
  output [7:0] soma,
  output [1:0] estado,
  output pronto
);

  wire bc_1_cac, bc_1_dec, bc_1_rac, bc_1_set, bo_1_zero;

  BC bc_1 (
    .inicioC(start), .zeroD(bo_1_zero), .clk(clk), .rst(rst), .set(bc_1_set), .rac(bc_1_rac), .dec(bc_1_dec),
    .cac(bc_1_cac), .pronto(pronto), .state(estado));
  BO bo_1 (
    .dec(bc_1_set), .set(bc_1_dec), .rst(rst), .cac(bc_1_cac), .clk(clk), .rac(bc_1_rac), .valor(valor),
    .zero(bo_1_zero), .overflow(overflow), .soma(soma));
endmodule

module BC (
  input  inicioC,
  input  zeroD,
  input  clk,
  input  rst,
  output set,
  output rac,
  output dec,
  output cac,
  output pronto,
  output [1:0] state
);

  wire and_1_out, d0_1_saida;

  and and_1 (and_1_out, ~state[1], state[0]);  // AND_Gate
  D0 d0_1 (.D(zeroD), .C(inicioC), .B(state[0]), .A(state[1]), .saida(d0_1_saida));
  D_Flip_Flop A (.D(and_1_out), .clk(clk), .Q(state[1]), .reset(rst));  // open: Qn, preset
  D_Flip_Flop B (.D(d0_1_saida), .clk(clk), .Q(state[0]), .reset(rst));  // open: Qn, preset
  and and_2 (rac, ~state[1], ~state[0]);  // AND_Gate
  and and_3 (cac, state[1], ~state[0]);  // AND_Gate
  xor xor_1 (pronto, state[1], state[0]);

  assign dec = cac;
  assign set = rac;

  // Notes on the sheet:
  //   !AB
endmodule

module BO (
  input  dec,
  input  set,
  input  rst,
  input  cac,
  input  clk,
  input  rac,
  input  [7:0] valor,
  output zero,
  output overflow,
  output [7:0] soma
);

  wire cont_q;
  wire [7:0] acum_q;

  Register acum (.D(soma), .en(cac), .clk(clk), .Q(acum_q), .clr(rac));
  Adder adder_1 (.a(acum_q), .b(valor), .out(soma), .cout(overflow));  // open: cin
  Register #(.width(1)) cont (.D(dec), .en(set), .clk(clk), .Q(cont_q), .clr(rst));
  not not_1 (zero, cont_q);
endmodule

module main (
  input  in_1,
  input  in_2,
  input  [7:0] in_3,
  output [7:0] out_4,
  output [1:0] out_5
);

  wire clock_1_out, project_1_overflow, project_1_pronto;

  Clock clock_1 (.out(clock_1_out));
  LED led_1 (.in(project_1_overflow));
  Project project_1 (
    .rst(in_1), .clk(clock_1_out), .start(in_2), .valor(in_3), .overflow(project_1_overflow), .soma(out_4),
    .estado(out_5), .pronto(project_1_pronto));
  LED led_2 (.in(project_1_pronto));
endmodule

module D0 (
  input  D,
  input  C,
  input  B,
  input  A,
  output saida
);

  wire and_1_out, and_2_out, and_3_out, and_4_out, and_5_out, and_6_out, and_7_out, and_8_out;

  and and_1 (and_1_out, ~A, ~B, C, ~D);  // AND_Gate
  and and_2 (and_2_out, ~A, ~B, C, D);  // AND_Gate
  and and_3 (and_3_out, ~A, B, ~C, D);  // AND_Gate
  and and_4 (and_4_out, ~A, B, C, D);  // AND_Gate
  and and_5 (and_5_out, A, ~B, ~C, ~D);  // AND_Gate
  and and_6 (and_6_out, A, ~B, ~C, D);  // AND_Gate
  and and_7 (and_7_out, A, ~B, C, ~D);  // AND_Gate
  and and_8 (and_8_out, A, ~B, C, D);  // AND_Gate
  or or_1 (saida, and_1_out, and_2_out, and_3_out, and_4_out, and_5_out, and_6_out, and_7_out, and_8_out);
endmodule
